# Fritzing sketch schematic (saved by Fritzing 0.9.3b)
breadboards: 1

parts:
  Part1 = Arduino Uno (Rev3) - ICSP
  J1 = Basic Force Sensing Resistor (FSR) [package=THT]
  R1 = Resistor [tolerance=±5% resistance=4.7k package="0603 [SMD]"]
  J2 = Basic Force Sensing Resistor (FSR) [package=THT]
  R2 = Resistor [tolerance=±5% resistance=4.7k package="0603 [SMD]"]
  J3 = Basic Force Sensing Resistor (FSR) [package=THT]
  R3 = Resistor [tolerance=±5% resistance=4.7k package="0603 [SMD]"]
  J4 = Basic Force Sensing Resistor (FSR) [package=THT]
  R4 = Resistor [tolerance=±5% resistance=4.7k package="0603 [SMD]"]
  J7 = Basic Force Sensing Resistor (FSR) [package=THT]
  R7 = Resistor [tolerance=±5% resistance=4.7k package="0603 [SMD]"]
  J8 = Basic Force Sensing Resistor (FSR) [package=THT]
  R8 = Resistor [tolerance=±5% resistance=4.7k package="0603 [SMD]"]

nets:
  N1: Part1.A0, J1.pin_0, R1.Pin_1
  N2: Part1.A1, J2.pin_0, R2.Pin_1
  N3: Part1.A2, J3.pin_0, R3.Pin_1
  N4: Part1.A3, J4.pin_0, R4.Pin_1
  N5: Part1.A4/SDA, J8.pin_0, R8.Pin_1
  N6: Part1.A5/SCL, J7.pin_0, R7.Pin_1
  N7: Part1.5V, J1.pin_1, J2.pin_1, J3.pin_1, J4.pin_1, J7.pin_1, J8.pin_1
  N8: Part1.GND, R1.Pin_0, R2.Pin_0, R3.Pin_0, R4.Pin_0, R7.Pin_0, R8.Pin_0
